// Logisim project bird.circ as structural Verilog: 4 circuits, main circuit bird
// Register Bank
module register_bank (
  input  [2:0] Reg_select,
  input  Reg_load,
  input  clock,
  input  [15:0] Data_in,
  input  sp_plus_plus,
  input  sp_minus_minus,
  output [15:0] dout0,
  output [15:0] dout1,
  output [15:0] dout2,
  output [15:0] dout3,
  output [15:0] dout4,
  output [15:0] dout5,
  output [15:0] dout6,
  output [15:0] dout7
);

  wire and_1_out, and_2_out, and_3_out, and_4_out, and_5_out, and_6_out, and_7_out, and_8_out, and_9_out,
       decoder_1_out0, decoder_1_out1, decoder_1_out2, decoder_1_out3, decoder_1_out4, decoder_1_out5,
       decoder_1_out6, decoder_1_out7, or_1_out;
  wire [15:0] adder_1_out, multiplexer_1_out;

  Decoder #(.select(3), .enable("false")) decoder_1 (
    .out0(decoder_1_out0), .out1(decoder_1_out1), .out2(decoder_1_out2), .out3(decoder_1_out3),
    .out4(decoder_1_out4), .out5(decoder_1_out5), .out6(decoder_1_out6), .out7(decoder_1_out7),
    .sel(Reg_select));
  and and_1 (and_1_out, decoder_1_out0, Reg_load);
  and and_2 (and_2_out, decoder_1_out1, Reg_load);
  and and_3 (and_3_out, decoder_1_out2, Reg_load);
  and and_4 (and_4_out, decoder_1_out3, Reg_load);
  and and_5 (and_5_out, decoder_1_out4, Reg_load);
  and and_6 (and_6_out, decoder_1_out5, Reg_load);
  and and_7 (and_7_out, decoder_1_out6, Reg_load);
  and and_8 (and_8_out, decoder_1_out7, Reg_load);
  Register #(.width(16)) register_1 (.D(Data_in), .en(and_1_out), .Q(dout0), .clk(clock));  // open: clr
  Register #(.width(16)) register_2 (.D(Data_in), .en(and_2_out), .Q(dout1), .clk(clock));  // open: clr
  Register #(.width(16)) register_3 (.D(Data_in), .en(and_3_out), .Q(dout2), .clk(clock));  // open: clr
  Register #(.width(16)) register_4 (.D(Data_in), .en(and_4_out), .Q(dout3), .clk(clock));  // open: clr
  Register #(.width(16)) register_5 (.D(Data_in), .en(and_5_out), .Q(dout4), .clk(clock));  // open: clr
  Register #(.width(16)) register_6 (.D(Data_in), .en(and_6_out), .Q(dout5), .clk(clock));  // open: clr
  Register #(.width(16)) register_7 (.D(Data_in), .en(and_7_out), .Q(dout6), .clk(clock));  // open: clr
  Register #(.width(16)) register_8 (.D(Data_in), .en(and_8_out), .clk(clock));  // open: Q, clr
  Adder #(.width(16)) adder_1 (.a(dout7), .b(multiplexer_1_out), .out(adder_1_out));  // open: cin, cout
  Register #(.width(16)) register_9 (.D(adder_1_out), .en(or_1_out), .Q(dout7), .clk(clock));  // open: clr
  or or_1 (or_1_out, sp_plus_plus, sp_minus_minus);
  and and_9 (and_9_out, ~sp_minus_minus, sp_plus_plus);  // AND_Gate
  Multiplexer #(.width(16), .enable("false")) multiplexer_1 (
    .in0({16{1'b1}}), .in1(16'h1), .out(multiplexer_1_out), .sel(and_9_out));
endmodule

module ALU (
  input  [15:0] Din1,
  input  [15:0] Din2,
  input  [5:0] ALUOP,
  output out_4,
  output [15:0] result
);

  wire [15:0] adder_1_out, adder_2_out, and_1_out, multiplexer_1_out, not_1_out, or_1_out, subtractor_1_out,
       subtractor_2_out, xor_1_out;

  Adder #(.width(16)) adder_1 (.a(Din1), .b(Din2), .out(adder_1_out));  // open: cin, cout
  Subtractor #(.width(16)) subtractor_1 (.a(Din1), .b(Din2), .out(subtractor_1_out));  // open: bin, bout
  assign and_1_out = Din1 & Din2;  // AND_Gate and_1, 16 bits wide
  assign or_1_out = Din1 | Din2;  // OR_Gate or_1, 16 bits wide
  assign xor_1_out = Din1 ^ Din2;  // XOR_Gate xor_1, 16 bits wide
  assign not_1_out = ~Din2;  // NOT_Gate not_1, 16 bits wide
  Adder #(.width(16)) adder_2 (.a(Din2), .b(16'h1), .out(adder_2_out));  // open: cin, cout
  Subtractor #(.width(16)) subtractor_2 (.a(Din2), .b(16'h1), .out(subtractor_2_out));  // open: bin, bout
  Multiplexer #(.select(3), .width(16)) multiplexer_1 (
    .in0(not_1_out), .in1(Din2), .in2(adder_2_out), .in3(subtractor_2_out), .out(multiplexer_1_out),
    .sel(ALUOP[2:0]));  // open: in4, in5, in6, in7, en
  Multiplexer #(.select(3), .width(16)) multiplexer_2 (
    .in0(adder_1_out), .in1(subtractor_1_out), .in2(and_1_out), .in3(or_1_out), .in4(xor_1_out),
    .in7(multiplexer_1_out), .out(result), .sel(ALUOP[5:3]));  // open: in5, in6, en
  nor zf (out_4, result[0], result[1], result[2], result[3], result[4], result[5], result[6], result[7], result[8], result[9], result[10], result[11], result[12], result[13], result[14], result[15]);
endmodule

// Control Unit
module control_unit (
  input  [3:0] address,
  input  ZF,
  input  clock,
  output sp_minus_minus,
  output ARMUXBit2,
  output sp_plus_plus,
  output DataMux,
  output PCMUX,
  output IRLD,
  output MEMLD,
  output MUX,
  output ZFLD,
  output REGLD,
  output PCLD,
  output PCINC,
  output ARMUXBit1
);

  wire fetch, nextAddr0, nextAddr1, nextAddr2, nextAddr3;
  wire [1:1] and_1_out;
  wire [3:0] multiplexer_1_out, multiplexer_2_out, register_1_q;

  and and_1 (and_1_out[1], ~address[0], ~address[1], address[2], ~address[3]);  // AND_Gate
  Multiplexer #(.select(2), .width(4)) multiplexer_1 (
    .in0(address), .in1(address), .in2(4'b0000), .in3(4'b0101), .out(multiplexer_1_out),
    .sel({and_1_out[1], ZF}));  // open: en
  Multiplexer #(.width(4)) multiplexer_2 (
    .in0({nextAddr3, nextAddr2, nextAddr1, nextAddr0}), .in1(multiplexer_1_out), .out(multiplexer_2_out),
    .sel(fetch));  // open: en
  Register #(.width(4)) register_1 (.D(multiplexer_2_out), .en(1'b1), .Q(register_1_q), .clk(clock));  // open: clr
  ROM #(.addrWidth(4), .dataWidth(18)) rom_1 (
    .addr(register_1_q),
    .data({fetch, PCLD, PCINC, ARMUXBit1, REGLD, ZFLD, MUX, MEMLD, IRLD, PCMUX, DataMux, sp_plus_plus, sp_minus_minus, nextAddr3, nextAddr2, nextAddr1, nextAddr0, ARMUXBit2}));  // open: sel

  // Notes on the sheet:
  //   contents of rom_1 (hex, n*v repeats v):
  //   28200 a800 6800 4400 0 10000 0 3000 10021 58 104a1 5c a001 2101
endmodule

module bird (
);

  wire alu_1_out_4, ARMUXbit1, ARMUXbit2, clk, DataMux, IRLD, MEMLD, MUX, PCINC, PCLD, PCMUX, REGLD,
       sp_minus_minus, sp_plus_plus, zf, ZFLD;
  wire [3:0] opcode, register_bank_1_dout0_2;
  wire [5:0] AluOp, offset;
  wire [11:0] adder_1_out, address, mem_addr, multiplexer_2_out, partial_instruction, PCValue,
       register_bank_1_dout0;
  wire [15:0] alu_1_result, Data_in, Dout, multiplexer_1_out, register_bank_1_dout1, register_bank_1_dout2,
       register_bank_1_dout3, register_bank_1_dout4, register_bank_1_dout5, register_bank_1_dout6, SP;
  wire [15:12] multiplexer_6_out;

  Multiplexer #(.width(16), .enable("false")) multiplexer_1 (
    .in0(Dout), .in1({4'b0000, PCValue}), .out(multiplexer_1_out), .sel(DataMux));
  Multiplexer #(.width(12)) multiplexer_2 (
    .in0(adder_1_out), .in1(partial_instruction), .out(multiplexer_2_out), .sel(PCMUX));  // open: en
  Counter #(.width(12), .max('hfff)) counter_1 (
    .load(PCLD), .D(multiplexer_2_out), .count(PCINC), .Q(PCValue), .clk(clk));  // open: carry, clr
  Adder #(.width(12)) adder_1 (.a(PCValue), .b({AluOp, offset}), .out(adder_1_out));  // open: cin, cout
  Clock clock_1 (.out(clk));
  RAM #(.addrWidth(12), .dataWidth(16), .bus("separate")) ram_1 (
    .addr(address), .din(multiplexer_1_out), .data({opcode, partial_instruction}), .str(MEMLD), .clk(clk));  // open: sel, ld, clr
  Multiplexer #(.select(2), .width(12)) multiplexer_3 (
    .in0(PCValue), .in1(mem_addr), .in2(SP[11:0]), .out(address), .sel({ARMUXbit2, ARMUXbit1}));  // open: in3, en
  register_bank register_bank_1 (
    .Reg_select(offset[2:0]), .Reg_load(REGLD), .Data_in(Data_in),
    .dout0({register_bank_1_dout0_2, register_bank_1_dout0}), .dout1(register_bank_1_dout1),
    .dout2(register_bank_1_dout2), .dout3(register_bank_1_dout3), .dout4(register_bank_1_dout4),
    .dout5(register_bank_1_dout5), .dout6(register_bank_1_dout6), .dout7(SP), .clock(clk),
    .sp_plus_plus(sp_plus_plus), .sp_minus_minus(sp_minus_minus));
  Register #(.width(1)) register_1 (.D(alu_1_out_4), .en(ZFLD), .Q(zf), .clk(clk));  // open: clr
  Hex_Digit_Display hex_digit_display_1 (.value(register_bank_1_dout0_2));  // open: dp
  Hex_Digit_Display hex_digit_display_2 (.value(register_bank_1_dout0[11:8]));  // open: dp
  Multiplexer #(.select(3), .width(16)) multiplexer_4 (
    .in0({register_bank_1_dout0_2, register_bank_1_dout0}), .in1(register_bank_1_dout1),
    .in2(register_bank_1_dout2), .in3(register_bank_1_dout3), .in4(register_bank_1_dout4),
    .in5(register_bank_1_dout5), .in6(register_bank_1_dout6), .in7(SP), .out(Dout), .sel(AluOp[2:0]));  // open: en
  Hex_Digit_Display hex_digit_display_3 (.value(register_bank_1_dout0[7:4]));  // open: dp
  Hex_Digit_Display hex_digit_display_4 (.value(register_bank_1_dout0[3:0]));  // open: dp
  ALU alu_1 (
    .Din1(Dout), .Din2({multiplexer_6_out, mem_addr}), .out_4(alu_1_out_4), .result(alu_1_result),
    .ALUOP(AluOp));
  Multiplexer #(.width(16)) multiplexer_5 (
    .in0(alu_1_result), .in1({opcode, partial_instruction}), .out(Data_in), .sel(MUX));  // open: en
  Multiplexer #(.select(3), .width(16)) multiplexer_6 (
    .in0({register_bank_1_dout0_2, register_bank_1_dout0}), .in1(register_bank_1_dout1),
    .in2(register_bank_1_dout2), .in3(register_bank_1_dout3), .in4(register_bank_1_dout4),
    .in5(register_bank_1_dout5), .in6(register_bank_1_dout6), .in7(SP), .out({multiplexer_6_out, mem_addr}),
    .sel(offset[5:3]));  // open: en
  control_unit control_unit_1 (
    .sp_minus_minus(sp_minus_minus), .sp_plus_plus(sp_plus_plus), .DataMux(DataMux), .PCMUX(PCMUX),
    .PCLD(PCLD), .ARMUXBit1(ARMUXbit1), .REGLD(REGLD), .MEMLD(MEMLD), .ZFLD(ZFLD), .address(opcode),
    .ARMUXBit2(ARMUXbit2), .ZF(zf), .clock(clk), .IRLD(IRLD), .PCINC(PCINC), .MUX(MUX));
  Register #(.width(12)) register_2 (.D(partial_instruction), .en(IRLD), .Q({AluOp, offset}), .clk(clk));  // open: clr

  // Other names for the same wires on the sheet: r1[2:0] = offset[2:0]; r3[2:0] = offset[5:3]; offset[11:6] = AluOp;
  //   r2[2:0] = AluOp[2:0]; whole_instruction[15:0] = {opcode, partial_instruction}
endmodule
