// Logisim project fish.circ as structural Verilog: 3 circuits, main circuit fish
// Register Bank
module register_bank (
  input  [2:0] Reg_select,
  input  Reg_load,
  input  clock,
  input  [15:0] Data_in,
  output [15:0] dout0,
  output [15:0] dout1,
  output [15:0] dout2,
  output [15:0] dout3,
  output [15:0] dout4,
  output [15:0] dout5,
  output [15:0] dout6,
  output [15:0] dout7
);

  wire and_1_out, and_2_out, and_3_out, and_4_out, and_5_out, and_6_out, and_7_out, and_8_out,
       decoder_1_out0, decoder_1_out1, decoder_1_out2, decoder_1_out3, decoder_1_out4, decoder_1_out5,
       decoder_1_out6, decoder_1_out7;

  Decoder #(.select(3), .enable("false")) decoder_1 (
    .out0(decoder_1_out0), .out1(decoder_1_out1), .out2(decoder_1_out2), .out3(decoder_1_out3),
    .out4(decoder_1_out4), .out5(decoder_1_out5), .out6(decoder_1_out6), .out7(decoder_1_out7),
    .sel(Reg_select));
  and and_1 (and_1_out, decoder_1_out0, Reg_load);
  and and_2 (and_2_out, decoder_1_out1, Reg_load);
  and and_3 (and_3_out, decoder_1_out2, Reg_load);
  and and_4 (and_4_out, decoder_1_out3, Reg_load);
  and and_5 (and_5_out, decoder_1_out4, Reg_load);
  and and_6 (and_6_out, decoder_1_out5, Reg_load);
  and and_7 (and_7_out, decoder_1_out6, Reg_load);
  and and_8 (and_8_out, decoder_1_out7, Reg_load);
  Register #(.width(16)) register_1 (.D(Data_in), .en(and_1_out), .Q(dout0), .clk(clock));  // open: clr
  Register #(.width(16)) register_2 (.D(Data_in), .en(and_2_out), .Q(dout1), .clk(clock));  // open: clr
  Register #(.width(16)) register_3 (.D(Data_in), .en(and_3_out), .Q(dout2), .clk(clock));  // open: clr
  Register #(.width(16)) register_4 (.D(Data_in), .en(and_4_out), .Q(dout3), .clk(clock));  // open: clr
  Register #(.width(16)) register_5 (.D(Data_in), .en(and_5_out), .Q(dout4), .clk(clock));  // open: clr
  Register #(.width(16)) register_6 (.D(Data_in), .en(and_6_out), .Q(dout5), .clk(clock));  // open: clr
  Register #(.width(16)) register_7 (.D(Data_in), .en(and_7_out), .Q(dout6), .clk(clock));  // open: clr
  Register #(.width(16)) register_8 (.D(Data_in), .en(and_8_out), .Q(dout7), .clk(clock));  // open: clr
endmodule

module ALU (
  input  [15:0] Din1,
  input  [15:0] Din2,
  input  [3:0] ALU_OP,
  output [15:0] zeroflag,
  output [15:0] result
);

  wire [15:0] adder_1_out, adder_2_out, and_1_out, not_1_out, or_1_out, subtractor_1_out, subtractor_2_out,
       xor_1_out;

  Adder #(.width(16)) adder_1 (.a(Din1), .b(Din2), .out(adder_1_out));  // open: cin, cout
  Subtractor #(.width(16)) subtractor_1 (.a(Din1), .b(Din2), .out(subtractor_1_out));  // open: bin, bout
  assign and_1_out = Din1 & Din2;  // AND_Gate and_1, 16 bits wide
  assign or_1_out = Din1 | Din2;  // OR_Gate or_1, 16 bits wide
  assign xor_1_out = Din1 ^ Din2;  // XOR_Gate xor_1, 16 bits wide
  assign not_1_out = ~Din1;  // NOT_Gate not_1, 16 bits wide
  Adder #(.width(16)) adder_2 (.a(Din1), .b(16'h1), .out(adder_2_out));  // open: cin, cout
  Subtractor #(.width(16)) subtractor_2 (.a(Din1), .b(16'h1), .out(subtractor_2_out));  // open: bin, bout
  Multiplexer #(.select(4), .width(16)) multiplexer_1 (
    .in0(adder_1_out), .in1(subtractor_1_out), .in2(and_1_out), .in3(or_1_out), .in4(xor_1_out),
    .in5(not_1_out), .in6(Din1), .in7(adder_2_out), .in8(subtractor_2_out), .out(result), .sel(ALU_OP));  // open: in9, in10, in11, in12, in13, in14, in15, en
  assign zeroflag = ~result;  // NOR_Gate nor_1, 16 bits wide NOR_Gate
endmodule

module fish (
  output [15:0] out_1
);

  wire clock_out;
  wire [1:0] PC_q;
  wire [12:0] rom_1_data;
  wire [15:0] alu_1_result, multiplexer_1_out, multiplexer_2_out, register_bank_1_dout0,
       register_bank_1_dout1, register_bank_1_dout2, register_bank_1_dout3, register_bank_1_dout4,
       register_bank_1_dout6, register_bank_1_dout7;

  Counter #(.width(2), .max('h3)) PC (.count(1'b1), .Q(PC_q), .clk(clock_out));  // open: load, D, carry, clr
  Clock clock (.out(clock_out));
  ROM #(.addrWidth(2), .dataWidth(13)) rom_1 (.addr(PC_q), .data(rom_1_data));  // open: sel
  register_bank register_bank_1 (
    .Reg_select(rom_1_data[2:0]), .Reg_load(1'b1), .Data_in(alu_1_result), .dout0(register_bank_1_dout0),
    .dout1(register_bank_1_dout1), .dout2(register_bank_1_dout2), .dout3(register_bank_1_dout3),
    .dout4(register_bank_1_dout4), .dout5(register_bank_1_dout4), .dout6(register_bank_1_dout6),
    .dout7(register_bank_1_dout7), .clock(clock_out));
  Multiplexer #(.select(3), .width(16)) multiplexer_1 (
    .in0(register_bank_1_dout0), .in1(register_bank_1_dout1), .in2(register_bank_1_dout2),
    .in3(register_bank_1_dout3), .in4(register_bank_1_dout4), .in5(register_bank_1_dout4),
    .in6(register_bank_1_dout6), .in7(register_bank_1_dout7), .out(multiplexer_1_out), .sel(rom_1_data[12:10]));  // open: en
  ALU alu_1 (
    .Din1(multiplexer_1_out), .Din2(multiplexer_2_out), .zeroflag(out_1), .result(alu_1_result),
    .ALU_OP(rom_1_data[6:3]));
  Multiplexer #(.select(3), .width(16)) multiplexer_2 (
    .in0(register_bank_1_dout0), .in1(register_bank_1_dout1), .in2(register_bank_1_dout2),
    .in3(register_bank_1_dout3), .in4(register_bank_1_dout4), .in5(register_bank_1_dout4),
    .in6(register_bank_1_dout6), .in7(register_bank_1_dout7), .out(multiplexer_2_out), .sel(rom_1_data[9:7]));  // open: en

  // Notes on the sheet:
  //   contents of rom_1 (hex, n*v repeats v):
  //   439 83a 503 c30
  //   Dist
  //   Dout[2:0]
  //   zeroFlag
  //   src1
  //   Dout[12:10]
  //   src2
  //   Dout[9:7]
  //   AluOP
  //   Dout[6:3]
endmodule
