// Logisim project frog.circ as structural Verilog: 5 circuits, main circuit frog
module ALU (
  input  [15:0] Din1,
  input  [15:0] Din2,
  input  [3:0] ALU_OP,
  output [15:0] zeroflag,
  output [15:0] result
);

  wire [15:0] adder_1_out, adder_2_out, and_1_out, not_1_out, or_1_out, subtractor_1_out, subtractor_2_out,
       xor_1_out;

  Adder #(.width(16)) adder_1 (.a(Din1), .b(Din2), .out(adder_1_out));  // open: cin, cout
  Subtractor #(.width(16)) subtractor_1 (.a(Din1), .b(Din2), .out(subtractor_1_out));  // open: bin, bout
  assign and_1_out = Din1 & Din2;  // AND_Gate and_1, 16 bits wide
  assign or_1_out = Din1 | Din2;  // OR_Gate or_1, 16 bits wide
  assign xor_1_out = Din1 ^ Din2;  // XOR_Gate xor_1, 16 bits wide
  assign not_1_out = ~Din1;  // NOT_Gate not_1, 16 bits wide
  Adder #(.width(16)) adder_2 (.a(Din1), .b(16'h1), .out(adder_2_out));  // open: cin, cout
  Subtractor #(.width(16)) subtractor_2 (.a(Din1), .b(16'h1), .out(subtractor_2_out));  // open: bin, bout
  Multiplexer #(.select(4), .width(16)) multiplexer_1 (
    .in0(adder_1_out), .in1(subtractor_1_out), .in2(and_1_out), .in3(or_1_out), .in4(xor_1_out),
    .in5(not_1_out), .in6(Din1), .in7(adder_2_out), .in8(subtractor_2_out), .out(result), .sel(ALU_OP));  // open: in9, in10, in11, in12, in13, in14, in15, en
  assign zeroflag = ~result;  // NOR_Gate nor_1, 16 bits wide NOR_Gate
endmodule

module frog (
  output [15:0] zeroFlag
);

  wire clock_1_out, control_unit_1_irld, control_unit_1_ld, control_unit_1_mux, control_unit_1_pcinc;
  wire [1:0] register_1_q;
  wire [3:0] program_counter_1_out_3, register_1_q_3;
  wire [7:2] register_1_q_2;
  wire [15:0] alu_1_result, multiplexer_1_out, multiplexer_2_out, multiplexer_3_out, register_bank_4_1_dout0,
       register_bank_4_1_dout1, register_bank_4_1_dout2, register_bank_4_1_dout3, rom_1_data;

  program_counter program_counter_1 (
    .increment(control_unit_1_pcinc), .out_3(program_counter_1_out_3), .clock(clock_1_out));
  ROM #(.addrWidth(4), .dataWidth(16)) rom_1 (.addr(program_counter_1_out_3), .data(rom_1_data));  // open: sel
  Clock clock_1 (.out(clock_1_out));
  register_bank_4 register_bank_4_1 (
    .Reg_select(register_1_q), .Reg_load(control_unit_1_ld), .Data_in(multiplexer_1_out),
    .dout0(register_bank_4_1_dout0), .dout1(register_bank_4_1_dout1), .dout2(register_bank_4_1_dout2),
    .dout3(register_bank_4_1_dout3), .in_3(clock_1_out));
  Multiplexer #(.width(16)) multiplexer_1 (
    .in0(alu_1_result), .in1(rom_1_data), .out(multiplexer_1_out), .sel(control_unit_1_mux));  // open: en
  Multiplexer #(.select(2), .width(16)) multiplexer_2 (
    .in0(register_bank_4_1_dout0), .in1(register_bank_4_1_dout1), .in2(register_bank_4_1_dout2),
    .in3(register_bank_4_1_dout3), .out(multiplexer_2_out), .sel(register_1_q_2[7:6]));  // open: en
  ALU alu_1 (
    .Din1(multiplexer_2_out), .Din2(multiplexer_3_out), .zeroflag(zeroFlag), .result(alu_1_result),
    .ALU_OP(register_1_q_3));
  Multiplexer #(.select(2), .width(16)) multiplexer_3 (
    .in0(register_bank_4_1_dout0), .in1(register_bank_4_1_dout1), .in2(register_bank_4_1_dout2),
    .in3(register_bank_4_1_dout3), .out(multiplexer_3_out), .sel(register_1_q_2[4:3]));  // open: en
  control_unit control_unit_1 (
    .address(rom_1_data[13:12]), .load(1'b1), .IRLD(control_unit_1_irld), .LD(control_unit_1_ld),
    .MUX(control_unit_1_mux), .PCINC(control_unit_1_pcinc), .in_3(clock_1_out));
  Register #(.width(12)) register_1 (
    .D(rom_1_data[11:0]), .en(control_unit_1_irld), .Q({register_1_q_3, register_1_q_2, register_1_q}),
    .clk(clock_1_out));  // open: clr

  // Notes on the sheet:
  //   contents of rom_1 (hex, n*v repeats v):
  //   2003 4 16c1 2000 3 1142 1782 1800
  //   Dist
  //   Dout[2:0]
  //   src1
  //   Dout[12:10]
  //   Dout[13:12]
  //   Dout[11:0]
  //   src2
  //   Dout[9:7]
  //   AluOP
  //   Dout[6:3]
endmodule

// register bank
module register_bank_4 (
  input  [1:0] Reg_select,
  input  Reg_load,
  input  in_3,
  input  [15:0] Data_in,
  output [15:0] dout0,
  output [15:0] dout1,
  output [15:0] dout2,
  output [15:0] dout3
);

  wire and_1_out, and_2_out, and_3_out, and_4_out, decoder_1_out0, decoder_1_out1, decoder_1_out2,
       decoder_1_out3;

  Decoder #(.select(2), .enable("false")) decoder_1 (
    .out0(decoder_1_out0), .out1(decoder_1_out1), .out2(decoder_1_out2), .out3(decoder_1_out3),
    .sel(Reg_select));
  and and_1 (and_1_out, decoder_1_out0, Reg_load);
  and and_2 (and_2_out, decoder_1_out1, Reg_load);
  and and_3 (and_3_out, decoder_1_out2, Reg_load);
  and and_4 (and_4_out, decoder_1_out3, Reg_load);
  Register #(.width(16)) register_1 (.D(Data_in), .en(and_1_out), .Q(dout0), .clk(in_3));  // open: clr
  Register #(.width(16)) register_2 (.D(Data_in), .en(and_2_out), .Q(dout1), .clk(in_3));  // open: clr
  Register #(.width(16)) register_3 (.D(Data_in), .en(and_3_out), .Q(dout2), .clk(in_3));  // open: clr
  Register #(.width(16)) register_4 (.D(Data_in), .en(and_4_out), .Q(dout3), .clk(in_3));  // open: clr
endmodule

// control unit
module control_unit (
  input  [1:0] address,
  input  load,
  input  in_3,
  output PCINC,
  output LD,
  output MUX,
  output IRLD
);

  wire [1:0] multiplexer_1_out, register_1_q;
  wire [4:4] rom_1_data;

  Multiplexer #(.width(2)) multiplexer_1 (
    .in0(2'b00), .in1(address), .out(multiplexer_1_out), .sel(rom_1_data[4]));  // open: en
  Register #(.width(2)) register_1 (.D(multiplexer_1_out), .en(load), .Q(register_1_q), .clk(in_3));  // open: clr
  ROM #(.addrWidth(2), .dataWidth(5)) rom_1 (
    .addr(register_1_q), .data({rom_1_data[4], IRLD, MUX, LD, PCINC}));  // open: sel

  // Notes on the sheet:
  //   contents of rom_1 (hex, n*v repeats v):
  //   19 2 7
endmodule

// PC
module program_counter (
  input  increment,
  input  clock,
  output [3:0] out_3
);

  wire [3:0] adder_1_out;

  Register #(.width(4)) register_1 (.D(adder_1_out), .en(increment), .Q(out_3), .clk(clock));  // open: clr
  Adder #(.width(4)) adder_1 (.a(4'b0001), .b(out_3), .out(adder_1_out));  // open: cin, cout
endmodule
