// Logisim project Logisim.circ as structural Verilog: 6 circuits, main circuit reptile_8
// Register Bank
module register_bank (
  input  [2:0] Reg_select,
  input  Reg_load,
  input  clock,
  input  [15:0] Data_in,
  output [15:0] dout0,
  output [15:0] dout1,
  output [15:0] dout2,
  output [15:0] dout3,
  output [15:0] dout4,
  output [15:0] dout5,
  output [15:0] dout6,
  output [15:0] dout7
);

  wire and_1_out, and_2_out, and_3_out, and_4_out, and_5_out, and_6_out, and_7_out, and_8_out,
       decoder_1_out0, decoder_1_out1, decoder_1_out2, decoder_1_out3, decoder_1_out4, decoder_1_out5,
       decoder_1_out6, decoder_1_out7;

  Decoder #(.select(3), .enable("false")) decoder_1 (
    .out0(decoder_1_out0), .out1(decoder_1_out1), .out2(decoder_1_out2), .out3(decoder_1_out3),
    .out4(decoder_1_out4), .out5(decoder_1_out5), .out6(decoder_1_out6), .out7(decoder_1_out7),
    .sel(Reg_select));
  and and_1 (and_1_out, decoder_1_out0, Reg_load);
  and and_2 (and_2_out, decoder_1_out1, Reg_load);
  and and_3 (and_3_out, decoder_1_out2, Reg_load);
  and and_4 (and_4_out, decoder_1_out3, Reg_load);
  and and_5 (and_5_out, decoder_1_out4, Reg_load);
  and and_6 (and_6_out, decoder_1_out5, Reg_load);
  and and_7 (and_7_out, decoder_1_out6, Reg_load);
  and and_8 (and_8_out, decoder_1_out7, Reg_load);
  Register #(.width(16)) register_1 (.D(Data_in), .en(and_1_out), .Q(dout0), .clk(clock));  // open: clr
  Register #(.width(16)) register_2 (.D(Data_in), .en(and_2_out), .Q(dout1), .clk(clock));  // open: clr
  Register #(.width(16)) register_3 (.D(Data_in), .en(and_3_out), .Q(dout2), .clk(clock));  // open: clr
  Register #(.width(16)) register_4 (.D(Data_in), .en(and_4_out), .Q(dout3), .clk(clock));  // open: clr
  Register #(.width(16)) register_5 (.D(Data_in), .en(and_5_out), .Q(dout4), .clk(clock));  // open: clr
  Register #(.width(16)) register_6 (.D(Data_in), .en(and_6_out), .Q(dout5), .clk(clock));  // open: clr
  Register #(.width(16)) register_7 (.D(Data_in), .en(and_7_out), .Q(dout6), .clk(clock));  // open: clr
  Register #(.width(16)) register_8 (.D(Data_in), .en(and_8_out), .Q(dout7), .clk(clock));  // open: clr
endmodule

// control unit
module control_unit (
  input  [1:0] address,
  input  load,
  input  in_3,
  output PCINC,
  output LD,
  output MUX,
  output IRLD
);

  wire [1:0] multiplexer_1_out, register_1_q;
  wire [4:4] rom_1_data;

  Multiplexer #(.width(2)) multiplexer_1 (
    .in0(2'b00), .in1(address), .out(multiplexer_1_out), .sel(rom_1_data[4]));  // open: en
  Register #(.width(2)) register_1 (.D(multiplexer_1_out), .en(load), .Q(register_1_q), .clk(in_3));  // open: clr
  ROM #(.addrWidth(2), .dataWidth(5)) rom_1 (
    .addr(register_1_q), .data({rom_1_data[4], IRLD, MUX, LD, PCINC}));  // open: sel

  // Notes on the sheet:
  //   contents of rom_1 (hex, n*v repeats v):
  //   19 2 7
endmodule

module reptile_8 (
  input  load
);

  wire ARMUX, clk, IRLD, MEMLD, MUX, PCINC, PCLD, REGLD, reptile_8_alu_1_out_4, zf, ZFLD;
  wire [2:0] opcode;
  wire [3:0] register_bank_1_dout0_2;
  wire [5:0] AluOp, offset;
  wire [11:0] adder_1_out, address, counter_1_q, mem_addr, partial_instruction, register_bank_1_dout0;
  wire [15:0] Data_in, Dout, register_bank_1_dout1, register_bank_1_dout2, register_bank_1_dout3,
       register_bank_1_dout4, register_bank_1_dout5, register_bank_1_dout6, register_bank_1_dout7,
       reptile_8_alu_1_result;
  wire [15:12] multiplexer_4_out;
  wire [15:15] whole_instruction;

  Counter #(.width(12), .max('hfff)) counter_1 (
    .load(PCLD), .D(adder_1_out), .count(PCINC), .Q(counter_1_q), .clk(clk));  // open: carry, clr
  Adder #(.width(12)) adder_1 (.a(counter_1_q), .b({AluOp, offset}), .out(adder_1_out));  // open: cin, cout
  Clock clock_1 (.out(clk));
  RAM #(.addrWidth(12), .dataWidth(16), .bus("separate")) ram_1 (
    .addr(address), .din(Dout), .data({whole_instruction[15], opcode, partial_instruction}), .str(MEMLD),
    .clk(clk));  // open: sel, ld, clr
  Multiplexer #(.width(12)) multiplexer_1 (.in0(counter_1_q), .in1(mem_addr), .out(address), .sel(ARMUX));  // open: en
  register_bank register_bank_1 (
    .Reg_select(offset[2:0]), .Reg_load(REGLD), .Data_in(Data_in),
    .dout0({register_bank_1_dout0_2, register_bank_1_dout0}), .dout1(register_bank_1_dout1),
    .dout2(register_bank_1_dout2), .dout3(register_bank_1_dout3), .dout4(register_bank_1_dout4),
    .dout5(register_bank_1_dout5), .dout6(register_bank_1_dout6), .dout7(register_bank_1_dout7), .clock(clk));
  Register #(.width(1)) register_1 (.D(reptile_8_alu_1_out_4), .en(ZFLD), .Q(zf), .clk(clk));  // open: clr
  Hex_Digit_Display hex_digit_display_1 (.value(register_bank_1_dout0_2));  // open: dp
  Hex_Digit_Display hex_digit_display_2 (.value(register_bank_1_dout0[11:8]));  // open: dp
  Multiplexer #(.select(3), .width(16)) multiplexer_2 (
    .in0({register_bank_1_dout0_2, register_bank_1_dout0}), .in1(register_bank_1_dout1),
    .in2(register_bank_1_dout2), .in3(register_bank_1_dout3), .in4(register_bank_1_dout4),
    .in5(register_bank_1_dout5), .in6(register_bank_1_dout6), .in7(register_bank_1_dout7), .out(Dout),
    .sel(AluOp[2:0]));  // open: en
  Hex_Digit_Display hex_digit_display_3 (.value(register_bank_1_dout0[3:0]));  // open: dp
  Hex_Digit_Display hex_digit_display_4 (.value(register_bank_1_dout0[7:4]));  // open: dp
  reptile_8_ALU reptile_8_alu_1 (
    .Din1(Dout), .Din2({multiplexer_4_out, mem_addr}), .out_4(reptile_8_alu_1_out_4),
    .result(reptile_8_alu_1_result), .ALUOP(AluOp));
  Multiplexer #(.width(16)) multiplexer_3 (
    .in0(reptile_8_alu_1_result), .in1({whole_instruction[15], opcode, partial_instruction}), .out(Data_in),
    .sel(MUX));  // open: en
  Multiplexer #(.select(3), .width(16)) multiplexer_4 (
    .in0({register_bank_1_dout0_2, register_bank_1_dout0}), .in1(register_bank_1_dout1),
    .in2(register_bank_1_dout2), .in3(register_bank_1_dout3), .in4(register_bank_1_dout4),
    .in5(register_bank_1_dout5), .in6(register_bank_1_dout6), .in7(register_bank_1_dout7),
    .out({multiplexer_4_out, mem_addr}), .sel(offset[5:3]));  // open: en
  control_unit_reptile control_unit_reptile_1 (
    .PCLD(PCLD), .PCINC(PCINC), .ARMUX(ARMUX), .REGLD(REGLD), .MEMLD(MEMLD), .MUX(MUX), .ZFLD(ZFLD),
    .load(load), .in_4(clk), .IRLD(IRLD), .address(opcode), .ZF(zf));
  Register #(.width(12)) register_2 (.D(partial_instruction), .en(IRLD), .Q({AluOp, offset}), .clk(clk));  // open: clr

  // Other names for the same wires on the sheet: r1[2:0] = offset[2:0]; r3[2:0] = offset[5:3]; offset[11:6] = AluOp;
  //   r2[2:0] = AluOp[2:0]; whole_instruction[14:0] = {opcode, partial_instruction}
endmodule

// Control Unit
module control_unit_reptile (
  input  [2:0] address,
  input  ZF,
  input  load,
  input  in_4,
  output PCLD,
  output PCINC,
  output ARMUX,
  output REGLD,
  output MEMLD,
  output MUX,
  output ZFLD,
  output IRLD
);

  wire [1:1] and_1_out;
  wire [2:0] multiplexer_1_out, multiplexer_2_out, register_1_q;
  wire [8:8] rom_1_data;

  and and_1 (and_1_out[1], ~address[0], ~address[1], address[2]);  // AND_Gate
  Multiplexer #(.select(2), .width(3)) multiplexer_1 (
    .in0(address), .in1(address), .in2(3'b000), .in3(3'b101), .out(multiplexer_1_out),
    .sel({and_1_out[1], ZF}));  // open: en
  Multiplexer #(.width(3)) multiplexer_2 (
    .in0(3'b000), .in1(multiplexer_1_out), .out(multiplexer_2_out), .sel(rom_1_data[8]));  // open: en
  Register #(.width(3)) register_1 (.D(multiplexer_2_out), .en(load), .Q(register_1_q), .clk(in_4));  // open: clr
  ROM #(.addrWidth(3), .dataWidth(9)) rom_1 (
    .addr(register_1_q), .data({rom_1_data[8], PCLD, PCINC, ARMUX, REGLD, ZFLD, MUX, MEMLD, IRLD}));  // open: sel

  // Notes on the sheet:
  //   contents of rom_1 (hex, n*v repeats v):
  //   141 54 34 22 0 80 0 18
endmodule

// ALU
module reptile_8_ALU (
  input  [15:0] Din1,
  input  [15:0] Din2,
  input  [5:0] ALUOP,
  output out_4,
  output [15:0] result
);

  wire [15:0] adder_1_out, adder_2_out, and_1_out, multiplexer_1_out, not_1_out, or_1_out, subtractor_1_out,
       subtractor_2_out, xor_1_out;

  Adder #(.width(16)) adder_1 (.a(Din1), .b(Din2), .out(adder_1_out));  // open: cin, cout
  Subtractor #(.width(16)) subtractor_1 (.a(Din1), .b(Din2), .out(subtractor_1_out));  // open: bin, bout
  assign and_1_out = Din1 & Din2;  // AND_Gate and_1, 16 bits wide
  assign or_1_out = Din1 | Din2;  // OR_Gate or_1, 16 bits wide
  assign xor_1_out = Din1 ^ Din2;  // XOR_Gate xor_1, 16 bits wide
  assign not_1_out = ~Din2;  // NOT_Gate not_1, 16 bits wide
  Adder #(.width(16)) adder_2 (.a(Din2), .b(16'h1), .out(adder_2_out));  // open: cin, cout
  Subtractor #(.width(16)) subtractor_2 (.a(Din2), .b(16'h1), .out(subtractor_2_out));  // open: bin, bout
  Multiplexer #(.select(3), .width(16)) multiplexer_1 (
    .in0(not_1_out), .in1(Din2), .in2(adder_2_out), .in3(subtractor_2_out), .out(multiplexer_1_out),
    .sel(ALUOP[2:0]));  // open: in4, in5, in6, in7, en
  Multiplexer #(.select(3), .width(16)) multiplexer_2 (
    .in0(adder_1_out), .in1(subtractor_1_out), .in2(and_1_out), .in3(or_1_out), .in4(xor_1_out),
    .in7(multiplexer_1_out), .out(result), .sel(ALUOP[5:3]));  // open: in5, in6, en
  nor zf (out_4, result[0], result[1], result[2], result[3], result[4], result[5], result[6], result[7], result[8], result[9], result[10], result[11], result[12], result[13], result[14], result[15]);
endmodule

module program_counter_reptile (
  input  increment,
  input  clock,
  output [3:0] out_3
);

  wire [3:0] adder_1_out;

  Register #(.width(4)) register_1 (.D(adder_1_out), .en(increment), .Q(out_3), .clk(clock));  // open: clr
  Adder #(.width(4)) adder_1 (.a(4'b0001), .b(out_3), .out(adder_1_out));  // open: cin, cout
endmodule
